# Fritzing sketch sensorboxfzz (saved by Fritzing 1.0.4)
breadboards: 1

parts:
  A1 = PMS5003
  A2 = PMS5003
  V2 = DC Power [voltage=12V internal_resistance=0.1Ω]
  A3 = Raspberry Pi 5
  A4 = 3 channel relay module
  WATER_PUMP1 = water pump/motor
  VALVE1 = Plastic Solenoid Valve
  V3 = DC Power Supply [voltage=12V internal_resistance=1Ω max_current=0.1A]
  V1 = DC Power Supply [voltage=12V internal_resistance=1Ω max_current=0.1A]
  U1 = SIP - 5 pins [chip_label=SPS30 package="SIP (Single Inline) [THT]"]

nets:
  5V: A1.Pin_1, A2.Pin_1, A3.5V, A3.Fan-5V, A4.Pin_5, A4.Pin_7, V1.Pin_2, U1.VCC
  GND: A1.Pin_2, A2.Pin_2, V2.V+, A3.GND, A4.Pin_1, A4.Pin_6, WATER_PUMP1.pin_1, VALVE1.no_name_yet#2, V3.Pin_1, V1.Pin_1, U1.GND
  N1: A1.Pin_3, A1.Pin_6, A2.Pin_3, A2.Pin_6, A3.3V3
  N2: A1.Pin_4, A3.GPIO14
  N3: A1.Pin_5, A3.GPIO15
  N4: A2.Pin_4, A3.GPIO27
  N5: A2.Pin_5, A3.GPIO17
  N6: V2.V-, A4.Pin_10, V3.Pin_2
  N7: A3.ID_SD, U1.TX
  N8: A3.ID_SC, U1.RX
  N9: A3.GPIO26, A4.Pin_2
  N10: A3.GPIO20, A4.Pin_3
  N11: A3.GPIO21, A4.Pin_4
  N12: A4.Pin_9, VALVE1.no_name_yet#1
  N13: A4.Pin_11, WATER_PUMP1.pin_2

custom parts:
  PMS5003: PMS5003 is a kind of digital and universal particle concentration sensor, which can be used to obtain the number of suspended particles in the air.
  Raspberry Pi 5: The RPi5, a faster version of the awesome Raspberry Pi4B ARM Board with 40 pin gpio.
  3 channel relay module: This product is 3 channel self-locking and interlocking relay function.Keep button on 3 second when set tirgger level. it will automatic switchover self-locking and interlock function. 3 channel self-locking function:Press the corresponding button,the corresppond relay on,press again,relay off. 3 channel interlock function:Press the corresponding button,the corresppond relay on,but other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
  water pump/motor: WATER PUMP BY ARDUBLOCKTR
  SIP - 5 pins: Sensirion SPS30 particle sensor
